// Digital circuit lab2_part1.dig as structural Verilog
module lab2_part1 (
  input  inA_0,
  input  inA_1,
  input  inA_2,
  input  inA_3,
  input  inB_0,
  input  inB_1,
  input  inB_2,
  input  inB_3,
  input  op,
  output out0,
  output out1,
  output out2,
  output out3,
  output overflow
);

  wire add_1_c_o, add_2_c_o, add_3_c_o, multiplexer_1_out, multiplexer_2_out, multiplexer_3_out,
       multiplexer_4_out, not_1_out, not_2_out, not_3_out, not_4_out, not_5_out, xnor_1_out, xor_1_out;

  Multiplexer multiplexer_1 (.sel(not_5_out), .in_0(not_1_out), .in_1(inB_0), .out(multiplexer_1_out));
  not not_1 (not_1_out, inB_0);
  Multiplexer multiplexer_2 (.sel(not_5_out), .in_0(not_2_out), .in_1(inB_1), .out(multiplexer_2_out));
  not not_2 (not_2_out, inB_1);
  Multiplexer multiplexer_3 (.sel(not_5_out), .in_0(not_3_out), .in_1(inB_2), .out(multiplexer_3_out));
  not not_3 (not_3_out, inB_2);
  Multiplexer multiplexer_4 (.sel(not_5_out), .in_0(not_4_out), .in_1(inB_3), .out(multiplexer_4_out));
  not not_4 (not_4_out, inB_3);
  not not_5 (not_5_out, op);
  Add add_1 (.a(inA_0), .b(multiplexer_1_out), .c_i(op), .s(out0), .c_o(add_1_c_o));
  xnor xnor_1 (xnor_1_out, multiplexer_4_out, inA_3);
  xor xor_1 (xor_1_out, inA_3, out3);
  Add add_2 (.a(inA_1), .b(multiplexer_2_out), .c_i(add_1_c_o), .s(out1), .c_o(add_2_c_o));
  Add add_3 (.a(inA_2), .b(multiplexer_3_out), .c_i(add_2_c_o), .s(out2), .c_o(add_3_c_o));
  Add add_4 (.a(inA_3), .b(multiplexer_4_out), .c_i(add_3_c_o), .s(out3));  // open: c_o
  and and_1 (overflow, xnor_1_out, xor_1_out);

  // Notes on the sheet:
  //   Interface (do not edit the content inside this box)
  //   Inputs
  //   Result of doing the addition (op=0) / subtraction (op=1) and overflow bit:
  //   Output number (in 2's complement)
  //   First Number (in 2's complement)
  //   Second number (in 2's complement)
endmodule

/* Test case grading:
inA_0 inA_1 inA_2 inA_3 inB_0 inB_1 inB_2 inB_3 op out0 out1 out2 out3 overflow 

 0 0 0 0 0 0 0 0 0 0 0 0 0 0
 0 0 0 0 0 0 0 0 1 0 0 0 0 0
 0 0 0 0 0 0 0 1 0 0 0 0 1 0
 0 0 0 0 0 0 0 1 1 0 0 0 1 1
 0 0 0 0 0 0 1 0 0 0 0 1 0 0
 0 0 0 0 0 0 1 0 1 0 0 1 1 0
 0 0 0 0 0 0 1 1 0 0 0 1 1 0
 0 0 0 0 0 0 1 1 1 0 0 1 0 0
 0 0 0 0 0 1 0 0 0 0 1 0 0 0
 0 0 0 0 0 1 0 0 1 0 1 1 1 0
 0 0 0 0 0 1 0 1 0 0 1 0 1 0
 0 0 0 0 0 1 0 1 1 0 1 1 0 0
 0 0 0 0 0 1 1 0 0 0 1 1 0 0
 0 0 0 0 0 1 1 0 1 0 1 0 1 0
 0 0 0 0 0 1 1 1 0 0 1 1 1 0
 0 0 0 0 0 1 1 1 1 0 1 0 0 0
 0 0 0 0 1 0 0 0 0 1 0 0 0 0
 0 0 0 0 1 0 0 0 1 1 1 1 1 0
 0 0 0 0 1 0 0 1 0 1 0 0 1 0
 0 0 0 0 1 0 0 1 1 1 1 1 0 0
 0 0 0 0 1 0 1 0 0 1 0 1 0 0
 0 0 0 0 1 0 1 0 1 1 1 0 1 0
 0 0 0 0 1 0 1 1 0 1 0 1 1 0
 0 0 0 0 1 0 1 1 1 1 1 0 0 0
 0 0 0 0 1 1 0 0 0 1 1 0 0 0
 0 0 0 0 1 1 0 0 1 1 0 1 1 0
 0 0 0 0 1 1 0 1 0 1 1 0 1 0
 0 0 0 0 1 1 0 1 1 1 0 1 0 0
 0 0 0 0 1 1 1 0 0 1 1 1 0 0
 0 0 0 0 1 1 1 0 1 1 0 0 1 0
 0 0 0 0 1 1 1 1 0 1 1 1 1 0
 0 0 0 0 1 1 1 1 1 1 0 0 0 0
 0 0 0 1 0 0 0 0 0 0 0 0 1 0
 0 0 0 1 0 0 0 0 1 0 0 0 1 0
 0 0 0 1 0 0 0 1 0 0 0 0 0 1
 0 0 0 1 0 0 0 1 1 0 0 0 0 0
 0 0 0 1 0 0 1 0 0 0 0 1 1 0
 0 0 0 1 0 0 1 0 1 0 0 1 0 1
 0 0 0 1 0 0 1 1 0 0 0 1 0 1
 0 0 0 1 0 0 1 1 1 0 0 1 1 0
 0 0 0 1 0 1 0 0 0 0 1 0 1 0
 0 0 0 1 0 1 0 0 1 0 1 1 0 1
 0 0 0 1 0 1 0 1 0 0 1 0 0 1
 0 0 0 1 0 1 0 1 1 0 1 1 1 0
 0 0 0 1 0 1 1 0 0 0 1 1 1 0
 0 0 0 1 0 1 1 0 1 0 1 0 0 1
 0 0 0 1 0 1 1 1 0 0 1 1 0 1
 0 0 0 1 0 1 1 1 1 0 1 0 1 0
 0 0 0 1 1 0 0 0 0 1 0 0 1 0
 0 0 0 1 1 0 0 0 1 1 1 1 0 1
 0 0 0 1 1 0 0 1 0 1 0 0 0 1
 0 0 0 1 1 0 0 1 1 1 1 1 1 0
 0 0 0 1 1 0 1 0 0 1 0 1 1 0
 0 0 0 1 1 0 1 0 1 1 1 0 0 1
 0 0 0 1 1 0 1 1 0 1 0 1 0 1
 0 0 0 1 1 0 1 1 1 1 1 0 1 0
 0 0 0 1 1 1 0 0 0 1 1 0 1 0
 0 0 0 1 1 1 0 0 1 1 0 1 0 1
 0 0 0 1 1 1 0 1 0 1 1 0 0 1
 0 0 0 1 1 1 0 1 1 1 0 1 1 0
 0 0 0 1 1 1 1 0 0 1 1 1 1 0
 0 0 0 1 1 1 1 0 1 1 0 0 0 1
 0 0 0 1 1 1 1 1 0 1 1 1 0 1
 0 0 0 1 1 1 1 1 1 1 0 0 1 0
 0 0 1 0 0 0 0 0 0 0 0 1 0 0
 0 0 1 0 0 0 0 0 1 0 0 1 0 0
 0 0 1 0 0 0 0 1 0 0 0 1 1 0
 0 0 1 0 0 0 0 1 1 0 0 1 1 1
 0 0 1 0 0 0 1 0 0 0 0 0 1 1
 0 0 1 0 0 0 1 0 1 0 0 0 0 0
 0 0 1 0 0 0 1 1 0 0 0 0 0 0
 0 0 1 0 0 0 1 1 1 0 0 0 1 1
 0 0 1 0 0 1 0 0 0 0 1 1 0 0
 0 0 1 0 0 1 0 0 1 0 1 0 0 0
 0 0 1 0 0 1 0 1 0 0 1 1 1 0
 0 0 1 0 0 1 0 1 1 0 1 0 1 1
 0 0 1 0 0 1 1 0 0 0 1 0 1 1
 0 0 1 0 0 1 1 0 1 0 1 1 1 0
 0 0 1 0 0 1 1 1 0 0 1 0 0 0
 0 0 1 0 0 1 1 1 1 0 1 1 0 0
 0 0 1 0 1 0 0 0 0 1 0 1 0 0
 0 0 1 0 1 0 0 0 1 1 1 0 0 0
 0 0 1 0 1 0 0 1 0 1 0 1 1 0
 0 0 1 0 1 0 0 1 1 1 1 0 1 1
 0 0 1 0 1 0 1 0 0 1 0 0 1 1
 0 0 1 0 1 0 1 0 1 1 1 1 1 0
 0 0 1 0 1 0 1 1 0 1 0 0 0 0
 0 0 1 0 1 0 1 1 1 1 1 1 0 0
 0 0 1 0 1 1 0 0 0 1 1 1 0 0
 0 0 1 0 1 1 0 0 1 1 0 0 0 0
 0 0 1 0 1 1 0 1 0 1 1 1 1 0
 0 0 1 0 1 1 0 1 1 1 0 0 1 1
 0 0 1 0 1 1 1 0 0 1 1 0 1 1
 0 0 1 0 1 1 1 0 1 1 0 1 1 0
 0 0 1 0 1 1 1 1 0 1 1 0 0 0
 0 0 1 0 1 1 1 1 1 1 0 1 0 0
 0 0 1 1 0 0 0 0 0 0 0 1 1 0
 0 0 1 1 0 0 0 0 1 0 0 1 1 0
 0 0 1 1 0 0 0 1 0 0 0 1 0 1
 0 0 1 1 0 0 0 1 1 0 0 1 0 0
 0 0 1 1 0 0 1 0 0 0 0 0 0 0
 0 0 1 1 0 0 1 0 1 0 0 0 1 0
 0 0 1 1 0 0 1 1 0 0 0 0 1 0
 0 0 1 1 0 0 1 1 1 0 0 0 0 0
 0 0 1 1 0 1 0 0 0 0 1 1 1 0
 0 0 1 1 0 1 0 0 1 0 1 0 1 0
 0 0 1 1 0 1 0 1 0 0 1 1 0 1
 0 0 1 1 0 1 0 1 1 0 1 0 0 0
 0 0 1 1 0 1 1 0 0 0 1 0 0 0
 0 0 1 1 0 1 1 0 1 0 1 1 0 1
 0 0 1 1 0 1 1 1 0 0 1 0 1 0
 0 0 1 1 0 1 1 1 1 0 1 1 1 0
 0 0 1 1 1 0 0 0 0 1 0 1 1 0
 0 0 1 1 1 0 0 0 1 1 1 0 1 0
 0 0 1 1 1 0 0 1 0 1 0 1 0 1
 0 0 1 1 1 0 0 1 1 1 1 0 0 0
 0 0 1 1 1 0 1 0 0 1 0 0 0 0
 0 0 1 1 1 0 1 0 1 1 1 1 0 1
 0 0 1 1 1 0 1 1 0 1 0 0 1 0
 0 0 1 1 1 0 1 1 1 1 1 1 1 0
 0 0 1 1 1 1 0 0 0 1 1 1 1 0
 0 0 1 1 1 1 0 0 1 1 0 0 1 0
 0 0 1 1 1 1 0 1 0 1 1 1 0 1
 0 0 1 1 1 1 0 1 1 1 0 0 0 0
 0 0 1 1 1 1 1 0 0 1 1 0 0 0
 0 0 1 1 1 1 1 0 1 1 0 1 0 1
 0 0 1 1 1 1 1 1 0 1 1 0 1 0
 0 0 1 1 1 1 1 1 1 1 0 1 1 0
 0 1 0 0 0 0 0 0 0 0 1 0 0 0
 0 1 0 0 0 0 0 0 1 0 1 0 0 0
 0 1 0 0 0 0 0 1 0 0 1 0 1 0
 0 1 0 0 0 0 0 1 1 0 1 0 1 1
 0 1 0 0 0 0 1 0 0 0 1 1 0 0
 0 1 0 0 0 0 1 0 1 0 1 1 1 0
 0 1 0 0 0 0 1 1 0 0 1 1 1 0
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*/
