// Digital circuit lab2_part2.dig as structural Verilog
module lab2_part2 (
  input  in0,
  input  in1,
  input  in2,
  input  in3,
  output seg_a,
  output seg_f,
  output seg_b,
  output seg_g,
  output seg_e,
  output seg_c,
  output seg_d,
  output seg_dp,
  output sign_a,
  output sign_f,
  output sign_b,
  output sign_g,
  output sign_e,
  output sign_c,
  output sign_d,
  output sign_dp
);

  wire add_2_c_o, add_3_c_o, add_4_c_o, multiplexer_1_out, multiplexer_2_out, multiplexer_3_out,
       multiplexer_4_out, not_1_out, not_2_out, not_3_out, not_4_out;
  wire [3:0] add_4_s;

  Multiplexer multiplexer_1 (.sel(in3), .in_0(in3), .in_1(not_1_out), .out(multiplexer_1_out));
  not not_1 (not_1_out, in3);
  Multiplexer multiplexer_2 (.sel(in3), .in_0(in2), .in_1(not_2_out), .out(multiplexer_2_out));
  not not_2 (not_2_out, in2);
  Multiplexer multiplexer_3 (.sel(in3), .in_0(in1), .in_1(not_3_out), .out(multiplexer_3_out));
  not not_3 (not_3_out, in1);
  Multiplexer multiplexer_4 (.sel(in3), .in_0(in0), .in_1(not_4_out), .out(multiplexer_4_out));
  not not_4 (not_4_out, in0);
  Seven_Seg seven_seg_1 (.a(1'b0), .b(1'b0), .c(1'b0), .d(1'b0), .e(1'b0), .f(1'b0), .g(in3), .dp(1'b0));
  Add add_1 (.a(multiplexer_1_out), .b(1'b0), .c_i(add_2_c_o), .s(add_4_s[3]));  // open: c_o
  Add add_2 (.a(multiplexer_2_out), .b(1'b0), .c_i(add_3_c_o), .s(add_4_s[2]), .c_o(add_2_c_o));
  Add add_3 (.a(multiplexer_3_out), .b(1'b0), .c_i(add_4_c_o), .s(add_4_s[1]), .c_o(add_3_c_o));
  Add add_4 (.a(multiplexer_4_out), .b(1'b0), .c_i(in3), .s(add_4_s[0]), .c_o(add_4_c_o));
  Seven_Seg seven_seg_2 (.a(seg_a), .b(seg_b), .c(seg_c), .d(seg_d), .e(seg_e), .f(seg_f), .g(seg_g), .dp(1'b0));
  Multiplexer #(.Selector_Bits(4), .Bits(7)) multiplexer_5 (
    .sel(add_4_s), .in_0(7'b1111110), .in_1(7'b0110000), .in_2(7'b1101101), .in_3(7'b1111001),
    .in_4(7'b0110011), .in_5(7'b1011011), .in_6(7'b1011111), .in_7(7'b1110000), .in_8({7{1'b1}}),
    .in_9({7{1'b0}}), .in_10({7{1'b0}}), .in_11({7{1'b0}}), .in_12({7{1'b0}}), .in_13({7{1'b0}}),
    .in_14({7{1'b0}}), .in_15({7{1'b0}}), .out({seg_a, seg_b, seg_c, seg_d, seg_e, seg_f, seg_g}));

  assign seg_dp = 1'b0;
  assign sign_a = 1'b0;
  assign sign_b = 1'b0;
  assign sign_c = 1'b0;
  assign sign_d = 1'b0;
  assign sign_dp = 1'b0;
  assign sign_e = 1'b0;
  assign sign_f = 1'b0;
  assign sign_g = in3;

  // Notes on the sheet:
  //   Interface (do not edit the content inside this box)
  //   Outputs:
  //   Inputs
  //   Sign
  //   Decimal Number
endmodule

/* Test case grading:
in3 in2 in1 in0  sign_a sign_b sign_c sign_d sign_e sign_f sign_g  seg_a seg_b seg_c seg_d seg_e seg_f seg_g
 0   0   0   0    0      0      0      0      0      0      0       1     1     1     1     1     1     0
*/
