// Digital circuit lab2_part3.dig as structural Verilog
module lab2_part3 (
  input  clk,
  input  in0,
  input  in1,
  input  in2,
  input  in3,
  input  sel_write_1,
  input  sel_write_0,
  input  sel_readA_1,
  input  sel_readA_0,
  input  sel_readB_1,
  input  sel_readB_0,
  input  op,
  output out0,
  output out1,
  output out2,
  output out3,
  output reg0_0,
  output reg0_1,
  output reg0_2,
  output reg0_3,
  output reg1_0,
  output reg1_1,
  output reg1_2,
  output reg1_3,
  output reg2_0,
  output reg2_1,
  output reg2_2,
  output reg2_3,
  output reg3_0,
  output reg3_1,
  output reg3_2,
  output reg3_3,
  output inA_0,
  output inA_1,
  output inA_2,
  output inA_3,
  output inB_0,
  output inB_1,
  output inB_2,
  output inB_3,
  output overflow
);

  wire add_1_c_o, add_2_c_o, add_3_c_o, decoder_1_out_0, decoder_1_out_1, decoder_1_out_2, decoder_1_out_3,
       multiplexer_3_out, multiplexer_4_out, multiplexer_5_out, multiplexer_6_out, not_1_out, not_2_out,
       not_3_out, not_4_out, not_5_out, xnor_1_out, xor_1_out;

  Seven_Seg_Hex seven_seg_hex_1 (.d({inA_3, inA_2, inA_1, inA_0}), .dp(1'b0));
  Seven_Seg_Hex seven_seg_hex_2 (.d({reg3_3, reg3_2, reg3_1, reg3_0}), .dp(1'b0));
  Seven_Seg_Hex seven_seg_hex_3 (.d({in3, in2, in1, in0}), .dp(1'b0));
  Decoder #(.Selector_Bits(2)) decoder_1 (
    .sel({sel_write_1, sel_write_0}), .out_0(decoder_1_out_0), .out_1(decoder_1_out_1),
    .out_2(decoder_1_out_2), .out_3(decoder_1_out_3));
  Register #(.Bits(4)) register_1 (
    .D({in3, in2, in1, in0}), .C(clk), .en(decoder_1_out_0), .Q({reg0_3, reg0_2, reg0_1, reg0_0}));
  Register #(.Bits(4)) register_2 (
    .D({in3, in2, in1, in0}), .C(clk), .en(decoder_1_out_1), .Q({reg1_3, reg1_2, reg1_1, reg1_0}));
  Register #(.Bits(4)) register_3 (
    .D({in3, in2, in1, in0}), .C(clk), .en(decoder_1_out_2), .Q({reg2_3, reg2_2, reg2_1, reg2_0}));
  Register #(.Bits(4)) register_4 (
    .D({in3, in2, in1, in0}), .C(clk), .en(decoder_1_out_3), .Q({reg3_3, reg3_2, reg3_1, reg3_0}));
  Seven_Seg_Hex seven_seg_hex_4 (.d({inB_3, inB_2, inB_1, inB_0}), .dp(1'b0));
  Multiplexer #(.Bits(4), .Selector_Bits(2)) multiplexer_1 (
    .sel({sel_readA_1, sel_readA_0}), .in_0({reg0_3, reg0_2, reg0_1, reg0_0}),
    .in_1({reg1_3, reg1_2, reg1_1, reg1_0}), .in_2({reg2_3, reg2_2, reg2_1, reg2_0}),
    .in_3({reg3_3, reg3_2, reg3_1, reg3_0}), .out({inA_3, inA_2, inA_1, inA_0}));
  Multiplexer #(.Selector_Bits(2), .Bits(4)) multiplexer_2 (
    .sel({sel_readB_1, sel_readB_0}), .in_0({reg0_3, reg0_2, reg0_1, reg0_0}),
    .in_1({reg1_3, reg1_2, reg1_1, reg1_0}), .in_2({reg2_3, reg2_2, reg2_1, reg2_0}),
    .in_3({reg3_3, reg3_2, reg3_1, reg3_0}), .out({inB_3, inB_2, inB_1, inB_0}));
  Seven_Seg_Hex seven_seg_hex_5 (.d({reg2_3, reg2_2, reg2_1, reg2_0}), .dp(1'b0));
  Seven_Seg_Hex seven_seg_hex_6 (.d({2'b00, sel_write_1, sel_write_0}), .dp(1'b0));
  not not_1 (not_1_out, inB_0);
  not not_2 (not_2_out, inB_1);
  not not_3 (not_3_out, inB_2);
  not not_4 (not_4_out, inB_3);
  Multiplexer multiplexer_3 (.sel(not_5_out), .in_0(not_1_out), .in_1(inB_0), .out(multiplexer_3_out));
  Multiplexer multiplexer_4 (.sel(not_5_out), .in_0(not_2_out), .in_1(inB_1), .out(multiplexer_4_out));
  Multiplexer multiplexer_5 (.sel(not_5_out), .in_0(not_3_out), .in_1(inB_2), .out(multiplexer_5_out));
  Multiplexer multiplexer_6 (.sel(not_5_out), .in_0(not_4_out), .in_1(inB_3), .out(multiplexer_6_out));
  not not_5 (not_5_out, op);
  Seven_Seg_Hex seven_seg_hex_7 (.d({2'b00, sel_readA_1, sel_readA_0}), .dp(1'b0));
  Add add_1 (.a(inA_0), .b(multiplexer_3_out), .c_i(op), .s(out0), .c_o(add_1_c_o));
  xnor xnor_1 (xnor_1_out, multiplexer_6_out, inA_3);
  xor xor_1 (xor_1_out, inA_3, out3);
  Seven_Seg_Hex seven_seg_hex_8 (.d({out3, out2, out1, out0}), .dp(1'b0));
  Add add_2 (.a(inA_1), .b(multiplexer_4_out), .c_i(add_1_c_o), .s(out1), .c_o(add_2_c_o));
  Add add_3 (.a(inA_2), .b(multiplexer_5_out), .c_i(add_2_c_o), .s(out2), .c_o(add_3_c_o));
  Add add_4 (.a(inA_3), .b(multiplexer_6_out), .c_i(add_3_c_o), .s(out3));  // open: c_o
  and and_1 (overflow, xnor_1_out, xor_1_out);
  Seven_Seg_Hex seven_seg_hex_9 (.d({reg1_3, reg1_2, reg1_1, reg1_0}), .dp(1'b0));
  Seven_Seg_Hex seven_seg_hex_10 (.d({2'b00, sel_readB_1, sel_readB_0}), .dp(1'b0));
  Seven_Seg_Hex seven_seg_hex_11 (.d({reg0_3, reg0_2, reg0_1, reg0_0}), .dp(1'b0));

  // Notes on the sheet:
  //   Interface (do not edit the content inside this box)
  //   Inputs
  //   Keypad
  //   Outputs
  //   Registers
  //   Values read into Adder/Subtractor input
  //   First Number (in 2's complement)
  //   Register 3
  //   NOTE: The display used is a simple hex display.
  //   For example, 2's complement number -1 (1111) would appear as F in the display.
  //   Synchronizing Clock
  //   Operator Bit Input
  //   Second Number (in 2's complement)
  //   Register Selection: Write-to
  //   Register 2
  //   Register Selection: Read-from
  //   Output Number (in 2's complement)
  //   input A register address:
  //   Register 1
  //   input B register address:
  //   Register 0
endmodule

/* Test case grading:
clk	in3	in2	in1	in0	sel^write_1	sel^write_0	sel^readA_1	sel^readA_0	sel^readB_1	sel^readB_0	reg3_3	reg3_2	reg3_1	reg3_0	reg2_3	reg2_2	reg2_1	reg2_0	reg1_3	reg1_2	reg1_1	reg1_0	reg0_3	reg0_2	reg0_1	reg0_0	out3	out2	out1	out0	op	overflow
0	0	0	0	1	0	0	0	0	0	0	0	0	0	0	0	0	0	0	0	0	0	0	0	0	0	0	0	0	0	0	0	0
1	0	0	0	1	0	0	0	0	0	0	0	0	0	0	0	0	0	0	0	0	0	0	0	0	0	1	0	0	1	0	0	0
0	0	0	1	0	0	1	0	0	0	1	0	0	0	0	0	0	0	0	0	0	0	0	0	0	0	1	0	0	0	1	0	0
1	0	0	1	0	0	1	0	0	0	1	0	0	0	0	0	0	0	0	0	0	1	0	0	0	0	1	0	0	1	1	0	0
0	0	1	1	0	1	0	0	1	1	0	0	0	0	0	0	0	0	0	0	0	1	0	0	0	0	1	0	0	1	0	0	0
1	0	1	1	0	1	0	0	1	1	0	0	0	0	0	0	1	1	0	0	0	1	0	0	0	0	1	1	0	0	0	0	1
0	1	1	1	1	1	1	1	1	1	1	0	0	0	0	0	1	1	0	0	0	1	0	0	0	0	1	0	0	0	0	1	0
1	1	1	1	1	1	1	1	1	1	1	1	1	1	1	0	1	1	0	0	0	1	0	0	0	0	1	0	0	0	0	1	0
0	0	0	0	0	0	0	0	0	0	1	1	1	1	1	0	1	1	0	0	0	1	0	0	0	0	1	1	1	1	1	1	0
1	0	0	0	0	0	0	0	0	0	1	1	1	1	1	0	1	1	0	0	0	1	0	0	0	0	0	1	1	1	0	1	0
0	0	0	0	0	0	0	0	0	1	1	1	1	1	1	0	1	1	0	0	0	1	0	0	0	0	0	0	0	0	1	1	0
1	0	0	0	0	0	0	0	0	1	1	1	1	1	1	0	1	1	0	0	0	1	0	0	0	0	0	0	0	0	1	1	0
*/
